# Fritzing sketch MAM_Board_With_Silkscreen (saved by Fritzing 0.9.3b)
circuit board: 5.07147cm x 9.87699cm
breadboards: 1

parts:
  S3 = Momentary Switch [package=tactile-pth]
  S4 = Momentary Switch [package=tactile-pth]
  Pad9 = Pad [width=3.33498896303836 height=1.58788344941793 connect=center]
  Pad10 = Pad [width=3.33498896303836 height=1.58788344941793 connect=center]
  Pad11 = Pad [width=3.33498896303836 height=1.58788344941793 connect=center]
  Pad13 = Pad [width=3.33498896303836 height=1.58788344941793 connect=center]
  Pad14 = Pad [width=3.33498896303836 height=1.58788344941793 connect=center]
  Pad15 = Pad [width=3.33498896303836 height=1.58788344941793 connect=center]
  Pad16 = Pad [width=3.33498896303836 height=1.58788344941793 connect=center]
  Pad17 = Pad [width=3.33498896303836 height=1.58788344941793 connect=center]
  Pad18 = Pad [width=3.33498896303836 height=1.58788344941793 connect=center]
  Pad19 = Pad [width=3.33498896303836 height=1.58788344941793 connect=center]
  Pad20 = Pad [width=3.33498896303836 height=1.58788344941793 connect=center]
  Pad21 = Pad [width=3.33498896303836 height=1.58788344941793 connect=center]  # not connected
  J1 = female pin header, 6 pins [form="♀ (female)"]
  J2 = female pin header, 3 pins [form="♀ (female)"]
  J3 = female pin header, 6 pins [form="♀ (female)"]

nets:
  N1: S3.1, S4.1, Pad9.pad, Pad13.pad, Pad16.pad, J2.pin2
  N2: S3.4, J1.pin1, J3.pin1
  N3: S4.4, J1.pin3, J3.pin3
  N4: Pad10.pad, J1.pin2, J3.pin2
  N5: Pad11.pad, Pad15.pad, Pad18.pad, J2.pin1
  N6: Pad14.pad, Pad19.pad
  N7: Pad17.pad, Pad20.pad
  N8: J1.pin4, J3.pin4
  N9: J1.pin5, J3.pin5
  N10: J1.pin6, J3.pin6

notes:
  note direction of LED strips
  Digispark
